# Fritzing sketch GaN Circuit layout (saved by Fritzing 0.9.3b)

parts:
  Part1 = Arduino Uno (Rev3)
  VCC1 = Battery
  R2 = Resistor [tolerance=±5% resistance=220 package=THT]

nets:
  N1: Part1.A0, VCC1.+, R2.Pin_0
  N2: Part1.A1, Part1.GND, VCC1.-, R2.Pin_1

notes:
  Drain Sense
  Source Sense
  GaN device (modelled as a resistor)
  Source Force
  Drain Force
  Tied to common ground
